// Digital circuit Principal.dig as structural Verilog
module Principal (
  input  CLK,
  input  [2:0] PROG,
  input  CHEIO,
  input  TAMPA,
  input  LIGA,
  output ENCHER,
  output ESVAZIAR,
  output AGITAR,
  output GIRAR
);

  wire mef_mlr_1_suspender, RESET_out;
  wire [3:0] CONT_out;

  Reset #(.invertOutput("false")) RESET (.out(RESET_out));
  Counter #(.Bits(4)) CONT (.en(mef_mlr_1_suspender), .C(CLK), .clr(RESET_out), .out(CONT_out));  // open: ovf
  MEF_MLR mef_mlr_1 (
    .PROG(PROG), .CHEIO(CHEIO), .TAMPA(TAMPA), .LIGA(LIGA), .CLK(CLK), .RESET(RESET_out), .CK(CONT_out),
    .ENCHER(ENCHER), .ESVAZIAR(ESVAZIAR), .AGITAR(AGITAR), .GIRAR(GIRAR), .SUSPENDER(mef_mlr_1_suspender));
endmodule

/* Test case MLR:
CLK  LIGA   PROG   CHEIO  TAMPA  ENCHER   ESVAZIAR   AGITAR  GIRAR
C     0      X      0      0	  0	   0	      0	      0
*/
