// Digital circuit mlr_modularizada.dig as structural Verilog
module mlr_modularizada (
  input  C,
  input  CLK_PASSA,
  input  L,
  input  P0,
  input  P1,
  input  T,
  input  clk,
  output agi,
  output en,
  output es,
  output gi,
  output hold
);

  wire caixinhad0_1_d0, caixinhad1_1_d1, caixinhad2_1_d2, caixinhad3_1_d3, Z_0_n, Z_1_n, Z_2_n, Z_3_n;

  caixinhaD3 caixinhad3_1 (
    .C(C), .CLK(CLK_PASSA), .L(L), .P0(P0), .P1(P1), .T(T), .Z_0_n(Z_0_n), .Z_1_n(Z_1_n), .Z_2_n(Z_2_n),
    .Z_3_n(Z_3_n), .D3(caixinhad3_1_d3));
  caixinhaD2 caixinhad2_1 (
    .C(C), .CLK(CLK_PASSA), .L(L), .P0(P0), .P1(P1), .T(T), .Z_0_n(Z_0_n), .Z_1_n(Z_1_n), .Z_2_n(Z_2_n),
    .Z_3_n(Z_3_n), .D2(caixinhad2_1_d2));
  caixinhaD1 caixinhad1_1 (
    .C(C), .CLK(CLK_PASSA), .L(L), .T(T), .Z_0_n(Z_0_n), .Z_1_n(Z_1_n), .Z_2_n(Z_2_n), .Z_3_n(Z_3_n),
    .D1(caixinhad1_1_d1));
  caixinhaD0 caixinhad0_1 (
    .C(C), .CLK(CLK_PASSA), .L(L), .P0(P0), .P1(P1), .T(T), .Z_0_n(Z_0_n), .Z_1_n(Z_1_n), .Z_2_n(Z_2_n),
    .Z_3_n(Z_3_n), .D0(caixinhad0_1_d0));
  saidaAGI saidaagi_1 (
    .C(C), .CLK(CLK_PASSA), .L(L), .P0(P0), .P1(P1), .T(T), .Z_0_n(Z_0_n), .Z_1_n(Z_1_n), .Z_2_n(Z_2_n),
    .Z_3_n(Z_3_n), .agi(agi));
  saidaEN saidaen_1 (
    .C(C), .CLK(CLK_PASSA), .L(L), .P0(P0), .P1(P1), .T(T), .Z_0_n(Z_0_n), .Z_1_n(Z_1_n), .Z_2_n(Z_2_n),
    .Z_3_n(Z_3_n), .en(en));
  saidaES saidaes_1 (
    .C(C), .CLK(CLK_PASSA), .L(L), .P0(P0), .P1(P1), .T(T), .Z_0_n(Z_0_n), .Z_1_n(Z_1_n), .Z_2_n(Z_2_n),
    .Z_3_n(Z_3_n), .es(es));
  saidaGI saidagi_1 (
    .C(C), .CLK(CLK_PASSA), .L(L), .P0(P0), .P1(P1), .T(T), .Z_0_n(Z_0_n), .Z_1_n(Z_1_n), .Z_2_n(Z_2_n),
    .Z_3_n(Z_3_n), .gi(gi));
  clock_mlr clock_mlr_1 (.Q0(Z_0_n), .Q1(Z_1_n), .Q2(Z_2_n), .Q3(Z_3_n), .T(T), .Hold(hold));
  D_FF u_Z_3_n (.D(caixinhad3_1_d3), .C(clk), .Q(Z_3_n));  // open: nQ
  D_FF u_Z_2_n (.D(caixinhad2_1_d2), .C(clk), .Q(Z_2_n));  // open: nQ
  D_FF u_Z_1_n (.D(caixinhad1_1_d1), .C(clk), .Q(Z_1_n));  // open: nQ
  D_FF u_Z_0_n (.D(caixinhad0_1_d0), .C(clk), .Q(Z_0_n));  // open: nQ
endmodule
